# Fritzing sketch SmartVasePrototipo (saved by Fritzing 0.9.3b)
breadboards: 1

parts:
  Componente1 = Arduino Uno (Rev3)
  Modulo_receptor_do_sensor_de_úmidade = YL-83 Sensor de úmidade- Control Board
  PCB2 = RTC_DS1302_module
  1_Channel_Relay1 = 1 Channel Power Relay

nets:
  N1: Componente1.A0, Modulo_receptor_do_sensor_de_úmidade.AO
  N2: Componente1.D4, 1_Channel_Relay1.IN
  N3: Componente1.D5_PWM, PCB2.RST
  N4: Componente1.D6_PWM, PCB2.CLK
  N5: Componente1.D7, PCB2.DAT
  VCC: Componente1.5V, Modulo_receptor_do_sensor_de_úmidade.VCC, PCB2.VCC, 1_Channel_Relay1.VCC
  GND: Componente1.GND, Modulo_receptor_do_sensor_de_úmidade.GND, PCB2.GND, 1_Channel_Relay1.GND

notes:
  Modulo do sensor de úmidade
  Modulo relé 1 canal
  Relogio de tempo real

custom parts:
  YL-83 Sensor de úmidade- Control Board: The YL-83 is a rain sensor that has more resistance when dry and less resistance when wet. The module runs at 5V.
  RTC_DS1302_module: Arduino module DS1302 SPI Real Time Clock
  1 Channel Power Relay: A 1 channel power relay. The module operates at 5V.
